// Digital circuit And.dig as structural Verilog
module And (
  input  in_1,
  input  in_3,
  output out_2
);

  wire nand_1_out;

  nand nand_1 (nand_1_out, in_1, in_3);
  not not_1 (out_2, nand_1_out);
endmodule
