// Digital circuit And16.dig as structural Verilog
module And16 (
  input  a0,
  input  b0,
  input  a1,
  input  b1,
  input  a2,
  input  b2,
  input  a3,
  input  b3,
  input  a4,
  input  b4,
  input  a5,
  input  b5,
  input  a6,
  input  b6,
  input  a7,
  input  b7,
  input  a8,
  input  b8,
  input  a9,
  input  b9,
  input  a10,
  input  b10,
  input  a11,
  input  b11,
  input  a12,
  input  b12,
  input  a13,
  input  b13,
  input  a14,
  input  b14,
  input  a15,
  input  b15,
  output _0,
  output _1,
  output _2,
  output _3,
  output _4,
  output _5,
  output _6,
  output _7,
  output _8,
  output _9,
  output _10,
  output _11,
  output _12,
  output _13,
  output _14,
  output _15
);

  and and_1 (_0, a0, b0);
  and and_2 (_1, a1, b1);
  and and_3 (_2, a2, b2);
  and and_4 (_3, a3, b3);
  and and_5 (_4, a4, b4);
  and and_6 (_5, a5, b5);
  and and_7 (_6, a6, b6);
  and and_8 (_7, a7, b7);
  and and_9 (_8, a8, b8);
  and and_10 (_9, a9, b9);
  and and_11 (_10, a10, b10);
  and and_12 (_11, a11, b11);
  and and_13 (_12, a12, b12);
  and and_14 (_13, a13, b13);
  and and_15 (_14, a14, b14);
  and and_16 (_15, a15, b15);
endmodule
