// Digital circuit Mux16.dig as structural Verilog
module Mux16 (
  input  a0,
  input  b0,
  input  sel,
  input  a1,
  input  b1,
  input  a2,
  input  b2,
  input  a3,
  input  b3,
  input  a4,
  input  b4,
  input  a5,
  input  b5,
  input  a6,
  input  b6,
  input  a7,
  input  b7,
  input  a8,
  input  b8,
  input  a9,
  input  b9,
  input  a10,
  input  b10,
  input  a11,
  input  b11,
  input  a12,
  input  b12,
  input  a13,
  input  b13,
  input  a14,
  input  b14,
  input  a15,
  input  b15,
  output _0,
  output _1,
  output _2,
  output _3,
  output _4,
  output _5,
  output _6,
  output _7,
  output _8,
  output _9,
  output _10,
  output _11,
  output _12,
  output _13,
  output _14,
  output _15
);

  Multiplexer multiplexer_1 (.sel(sel), .in_0(a0), .in_1(b0), .out(_0));
  Multiplexer multiplexer_2 (.sel(sel), .in_0(a1), .in_1(b1), .out(_1));
  Multiplexer multiplexer_3 (.sel(sel), .in_0(a2), .in_1(b2), .out(_2));
  Multiplexer multiplexer_4 (.sel(sel), .in_0(a3), .in_1(b3), .out(_3));
  Multiplexer multiplexer_5 (.sel(sel), .in_0(a4), .in_1(b4), .out(_4));
  Multiplexer multiplexer_6 (.sel(sel), .in_0(a5), .in_1(b5), .out(_5));
  Multiplexer multiplexer_7 (.sel(sel), .in_0(a6), .in_1(b6), .out(_6));
  Multiplexer multiplexer_8 (.sel(sel), .in_0(a7), .in_1(b7), .out(_7));
  Multiplexer multiplexer_9 (.sel(sel), .in_0(a8), .in_1(b8), .out(_8));
  Multiplexer multiplexer_10 (.sel(sel), .in_0(a9), .in_1(b9), .out(_9));
  Multiplexer multiplexer_11 (.sel(sel), .in_0(a10), .in_1(b10), .out(_10));
  Multiplexer multiplexer_12 (.sel(sel), .in_0(a11), .in_1(b11), .out(_11));
  Multiplexer multiplexer_13 (.sel(sel), .in_0(a12), .in_1(b12), .out(_12));
  Multiplexer multiplexer_14 (.sel(sel), .in_0(a13), .in_1(b13), .out(_13));
  Multiplexer multiplexer_15 (.sel(sel), .in_0(a14), .in_1(b14), .out(_14));
  Multiplexer multiplexer_16 (.sel(sel), .in_0(a15), .in_1(b15), .out(_15));
endmodule
