// Digital circuit Not16.dig as structural Verilog
module Not16 (
  input  _0_2,
  input  _1_2,
  input  _2_2,
  input  _3_2,
  input  _4_2,
  input  _5_2,
  input  _6_2,
  input  _7_2,
  input  _8_2,
  input  _9_2,
  input  _10_2,
  input  _11_2,
  input  _12_2,
  input  _13_2,
  input  _14_2,
  input  _15_2,
  output _0,
  output _1,
  output _2,
  output _3,
  output _4,
  output _5,
  output _6,
  output _7,
  output _8,
  output _9,
  output _10,
  output _11,
  output _12,
  output _13,
  output _14,
  output _15
);

  not not_1 (_0, _0_2);
  not not_2 (_1, _1_2);
  not not_3 (_2, _2_2);
  not not_4 (_3, _3_2);
  not not_5 (_4, _4_2);
  not not_6 (_5, _5_2);
  not not_7 (_6, _6_2);
  not not_8 (_7, _7_2);
  not not_9 (_8, _8_2);
  not not_10 (_9, _9_2);
  not not_11 (_10, _10_2);
  not not_12 (_11, _11_2);
  not not_13 (_12, _12_2);
  not not_14 (_13, _13_2);
  not not_15 (_14, _14_2);
  not not_16 (_15, _15_2);
endmodule
