// Digital circuit Or.dig as structural Verilog
module Or (
  input  in_2,
  input  in_3,
  output out_1
);

  wire not_1_out, not_2_out;

  not not_1 (not_1_out, in_2);
  not not_2 (not_2_out, in_3);
  nand nand_1 (out_1, not_1_out, not_2_out);
endmodule
