// Digital circuit Or16.dig as structural Verilog
module Or16 (
  input  a0,
  input  b0,
  input  a1,
  input  b1,
  input  a2,
  input  b2,
  input  a3,
  input  b3,
  input  a4,
  input  b4,
  input  a5,
  input  b5,
  input  a6,
  input  b6,
  input  a7,
  input  b7,
  input  a8,
  input  b8,
  input  a9,
  input  b9,
  input  a10,
  input  b10,
  input  a11,
  input  b11,
  input  a12,
  input  b12,
  input  a13,
  input  b13,
  input  a14,
  input  b14,
  input  a15,
  input  b15,
  output _0,
  output _1,
  output _2,
  output _3,
  output _4,
  output _5,
  output _6,
  output _7,
  output _8,
  output _9,
  output _10,
  output _11,
  output _12,
  output _13,
  output _14,
  output _15
);

  or or_1 (_0, a0, b0);
  or or_2 (_1, a1, b1);
  or or_3 (_2, a2, b2);
  or or_4 (_3, a3, b3);
  or or_5 (_4, a4, b4);
  or or_6 (_5, a5, b5);
  or or_7 (_6, a6, b6);
  or or_8 (_7, a7, b7);
  or or_9 (_8, a8, b8);
  or or_10 (_9, a9, b9);
  or or_11 (_10, a10, b10);
  or or_12 (_11, a11, b11);
  or or_13 (_12, a12, b12);
  or or_14 (_13, a13, b13);
  or or_15 (_14, a14, b14);
  or or_16 (_15, a15, b15);
endmodule
