// Digital circuit Or8Way.dig as structural Verilog
module Or8Way (
  input  in0,
  input  in1,
  input  in2,
  input  in3,
  input  in4,
  input  in5,
  input  in6,
  input  in7,
  output out
);

  wire or_1_out, or_2_out, or_3_out, or_4_out, or_5_out, or_6_out;

  or or_1 (or_1_out, in0, in1);
  or or_2 (or_2_out, or_1_out, in2);
  or or_3 (or_3_out, or_2_out, in3);
  or or_4 (or_4_out, or_3_out, in4);
  or or_5 (or_5_out, or_4_out, in5);
  or or_6 (or_6_out, or_5_out, in6);
  or or_7 (out, or_6_out, in7);
endmodule
